# Fritzing sketch gakuchohai (saved by Fritzing 0.9.2b)
breadboards: 1

parts:
  R3 = Resistor [tolerance=±5% resistance=10k package=THT]
  R4 = Resistor [tolerance=±5% resistance=10k package=THT]
  R2 = Resistor [tolerance=±5% resistance=10k package=THT]
  R4_2 = Resistor [tolerance=±5% resistance=10k package=THT]
  Q3 = Basic FET P-Channel [package="TO220 [THT]"]
  Q4 = Basic FET P-Channel [package="TO220 [THT]"]
  Q1 = Basic FET N-Channel [package="TO220 [THT]"]
  Q2 = Basic FET N-Channel [package="TO220 [THT]"]
  M1 = female pin header, 2 pins [form="♀ (female)"]
  Q6 = Basic FET P-Channel [package="TO220 [THT]"]
  Q7 = Basic FET N-Channel [package="TO220 [THT]"]
  Q8 = Basic FET N-Channel [package="TO220 [THT]"]
  R5 = Resistor [tolerance=±5% resistance=10k package=THT]
  R6 = Resistor [tolerance=±5% resistance=10k package=THT]
  R7 = Resistor [tolerance=±5% resistance=10k package=THT]
  R8 = Resistor [tolerance=±5% resistance=10k package=THT]
  M2 = female pin header, 2 pins [form="♀ (female)"]
  Q9 = Basic FET P-Channel [package="TO220 [THT]"]
  Q10 = Basic FET P-Channel [package="TO220 [THT]"]
  Q11 = Basic FET N-Channel [package="TO220 [THT]"]
  Q12 = Basic FET N-Channel [package="TO220 [THT]"]
  R9 = Resistor [tolerance=±5% resistance=10k package=THT]
  R10 = Resistor [tolerance=±5% resistance=10k package=THT]
  R11 = Resistor [tolerance=±5% resistance=10k package=THT]
  R12 = Resistor [tolerance=±5% resistance=10k package=THT]
  M3 = female pin header, 2 pins [form="♀ (female)"]
  IC2 = IC, DIP package, 18 pins [chip_label=IC]
  <-_battery&switch = female pin header, 2 pins [form="♀ (female)"]
  J2 = female pin header, 8 pins [form="♀ (female)"]
  R13 = Resistor [tolerance=±5% resistance=220 package=THT]
  Q5 = Basic FET P-Channel [package="TO220 [THT]"]
  R15 = Resistor [tolerance=±5% resistance=220 package=THT]
  R17 = Resistor [tolerance=±5% resistance=220 package=THT]
  R19 = Resistor [tolerance=±5% resistance=470 package=THT]
  R20 = Resistor [tolerance=±5% resistance=470 package=THT]
  R18 = Resistor [tolerance=±5% resistance=470 package=THT]
  R21 = Resistor [tolerance=±5% resistance=470 package=THT]
  S1 = Toggle Switch [package=THT]
  U2 = Voltage Regulator - 5V [package="TO220 [THT]"]
  C3 = Ceramic Capacitor [capacitance=100nF package="100 mil [THT, multilayer]"]
  C4 = Electrolytic Capacitor [capacitance=1µF package="100 mil [THT, electrolytic]"]
  LED1 = LED - 5mm [color="Red (633nm)" package="5 mm [THT]"]

nets:
  N1: R3.Pin_0, R4.Pin_0, Q1.source, Q2.source, Q7.source, Q8.source, R5.Pin_0, R7.Pin_0, Q11.source, Q12.source, R9.Pin_0, R11.Pin_0, IC2.pin9, <-_battery&switch.pin2, J2.pin7, R13.Pin_0, R15.Pin_0, R17.Pin_0, R19.Pin_0, R20.Pin_0, R18.Pin_0, U2.GND, C3.1, C4.-, LED1.cathode
  N2: R3.Pin_1, Q1.gate, IC2.pin2, J2.pin2
  N3: R4.Pin_1, Q2.gate, IC2.pin1, J2.pin1
  N4: R2.Pin_0, Q3.gate, IC2.pin18
  N5: R2.Pin_1, R4_2.Pin_1, Q3.source, Q4.source, Q6.source, R6.Pin_1, R8.Pin_1, Q9.source, Q10.source, R10.Pin_1, R12.Pin_1, Q5.source, S1.L1, S1.COM, U2.output_voltage, C3.0
  N6: R4_2.Pin_0, Q4.gate, IC2.pin17
  N7: Q3.drain, Q1.drain, M1.pin1, R13.Pin_1
  N8: Q4.drain, Q2.drain, M1.pin2, R18.Pin_1
  N9: Q6.gate, R6.Pin_0, IC2.pin16
  N10: Q6.drain, Q8.drain, M2.pin1, R15.Pin_1
  N11: Q7.gate, R5.Pin_1, IC2.pin3, J2.pin3
  N12: Q7.drain, M2.pin2, Q5.drain, R19.Pin_1
  N13: Q8.gate, R7.Pin_1, IC2.pin4, J2.pin4
  N14: R8.Pin_0, IC2.pin15, Q5.gate
  N15: Q9.gate, R12.Pin_0, IC2.pin13
  N16: Q9.drain, Q11.drain, M3.pin2, R20.Pin_1
  N17: Q10.gate, R10.Pin_0, IC2.pin14
  N18: Q10.drain, Q12.drain, M3.pin1, R17.Pin_1
  N19: Q11.gate, R9.Pin_1, IC2.pin5, J2.pin5
  N20: Q12.gate, R11.Pin_1, IC2.pin6, J2.pin6
  N21: IC2.pin10, <-_battery&switch.pin1, S1.L2
  N22: J2.pin8, R21.Pin_0, U2.input_voltage, C4.+
  N23: R21.Pin_1, LED1.anode

notes:
  -
  5V
  signal
  +
